# Fritzing sketch ina219_hardware_mount (saved by Fritzing 0.9.2b)

parts:
  LOAD = INA219 DC Current Sensor Breakout
  Part1 = Arduino Uno (Rev3) - ICSP
  M1 = DC Motor
  LOAD_POWER_SUPPLY = 4 x AAA Battery Mount
  SHUNT = Resistor [tolerance=±1% resistance=0.01 power=100W package=THT]

nets:
  VCC: LOAD.VCC, Part1.VIN
  GND: LOAD.GND, Part1.GND, M1.pin_1, LOAD_POWER_SUPPLY.-
  N1: LOAD.SCL, Part1.A5/SCL
  N2: LOAD.SDA, Part1.A4/SDA
  N3: LOAD.Vin-2, M1.pin_2, SHUNT.Pin_0
  N4: LOAD.Vin+2, LOAD_POWER_SUPPLY.+, SHUNT.Pin_1

notes:
  External SHUNT
  ex: 20A, 75mV, 0.00375ohm

custom parts:
  INA219 DC Current Sensor Breakout: INA DC Current Sensor Breakout
